# Fritzing sketch MotionDetector_with_Buzzer (saved by Fritzing 0.9.3b)
breadboards: 1

parts:
  Part1 = Arduino Uno (Rev3)
  R1 = Resistor [tolerance=±5% resistance=330 package=THT]  # not connected
  LED2_-_Movement_indicator = LED - 5mm [color="Red (633nm)" package="5 mm [THT]"]
  Movement_buzzer = Piezo Speaker
  R2 = Resistor [tolerance=±5% resistance=330 package=THT]
  LED3 = smd LED [color="Red (633nm)" package="0603 [SMD]"]
  LED3_-_Power_light = smd LED [color="Red (633nm)" package="1206 [SMD]"]
  PIR1 = PIR sensor

nets:
  N1: Part1.D8, R2.Pin_0
  N2: Part1.D13/SCK, Movement_buzzer.pin2
  N3: Part1.D7, PIR1.SIG
  5V: Part1.5V, LED3.anode, LED3_-_Power_light.anode, PIR1.VDD
  GND: Part1.GND, LED2_-_Movement_indicator.cathode, Movement_buzzer.pin1, LED3.cathode, LED3_-_Power_light.cathode, PIR1.GND
  N4: LED2_-_Movement_indicator.anode, R2.Pin_1

notes:
  Circuit for pir_basic
